// Logisim project HDL_Project.circ as structural Verilog: 47 circuits, main circuit main
module main (
  input  [1:0] N,
  input  [3:0] Opcode,
  input  [15:0] A,
  input  [15:0] B,
  output [15:0] Result_Binary,
  output [15:0] Result_Signed,
  output [15:0] Result_Unsigned,
  output Carry,
  output Zero,
  output Overflow,
  output Negative
);

  Multi_Mode_ALU multi_mode_alu_1 (
    .N(N), .B(B), .A(A), .Opcode(Opcode), .Result(Result_Binary), .Carry(Carry), .Zero(Zero),
    .Overflow(Overflow), .Negative(Negative));

  assign Result_Signed = Result_Binary;
  assign Result_Unsigned = Result_Binary;

  // Notes on the sheet:
  //   0000 - ADD
  //   0001 - SUB
  //   0010 - AND
  //   0011 - OR
  //   0100 - XOR
  //   0 - 4bit
  //   0101 - NOT
  //   0110 - SHL
  //   0111 - SHR
  //   1000 - INC
  //   1001 - DEC
  //   1 - 8 bit
  //   2 - 16 bit
  //   Flags
endmodule

module Multi_Mode_ALU (
  input  [3:0] Opcode,
  input  [1:0] N,
  input  [15:0] A,
  input  [15:0] B,
  output [15:0] Result,
  output Carry,
  output Zero,
  output Overflow,
  output Negative
);

  wire alu_4bit_1_carry, alu_4bit_1_negative, alu_4bit_1_overflow, alu_4bit_1_zero, alu_8bit_1_carry,
       alu_8bit_1_negative, alu_8bit_1_overflow, alu_8bit_1_zero, alu_16bit_1_carry, alu_16bit_1_negative,
       alu_16bit_1_overflow, alu_16bit_1_zero;
  wire [3:0] alu_4bit_1_result;
  wire [7:0] alu_8bit_1_result;
  wire [15:0] alu_16bit_1_result, bit_extender_1_out, bit_extender_2_out;

  ALU_4Bit alu_4bit_1 (
    .Opcode(Opcode), .A(A[3:0]), .B(B[3:0]), .Carry(alu_4bit_1_carry), .Overflow(alu_4bit_1_overflow),
    .Result(alu_4bit_1_result), .Zero(alu_4bit_1_zero), .Negative(alu_4bit_1_negative));
  ALU_8Bit alu_8bit_1 (
    .Opcode(Opcode), .A(A[7:0]), .B(B[7:0]), .Carry(alu_8bit_1_carry), .Overflow(alu_8bit_1_overflow),
    .Result(alu_8bit_1_result), .Zero(alu_8bit_1_zero), .Negative(alu_8bit_1_negative));
  ALU_16Bit alu_16bit_1 (
    .Opcode(Opcode), .A(A), .B(B), .Carry(alu_16bit_1_carry), .Overflow(alu_16bit_1_overflow),
    .Result(alu_16bit_1_result), .Negative(alu_16bit_1_negative), .Zero(alu_16bit_1_zero));
  assign bit_extender_1_out = {{12{alu_4bit_1_result[3]}}, alu_4bit_1_result};  // Bit_Extender bit_extender_1
  assign bit_extender_2_out = {{8{alu_8bit_1_result[7]}}, alu_8bit_1_result};  // Bit_Extender bit_extender_2
  Multiplexer #(.select(2), .width(16)) multiplexer_1 (
    .in0(bit_extender_1_out), .in1(bit_extender_2_out), .in2(alu_16bit_1_result), .out(Result), .sel(N));  // open: in3
  Multiplexer #(.select(2)) multiplexer_2 (
    .in0(alu_4bit_1_carry), .in1(alu_8bit_1_carry), .in2(alu_16bit_1_carry), .out(Carry), .sel(N));  // open: in3
  Multiplexer #(.select(2)) multiplexer_3 (
    .in0(alu_4bit_1_zero), .in1(alu_8bit_1_zero), .in2(alu_16bit_1_zero), .out(Zero), .sel(N));  // open: in3
  Multiplexer #(.select(2)) multiplexer_4 (
    .in0(alu_4bit_1_overflow), .in1(alu_8bit_1_overflow), .in2(alu_16bit_1_overflow), .out(Overflow), .sel(N));  // open: in3
  Multiplexer #(.select(2)) multiplexer_5 (
    .in0(alu_4bit_1_negative), .in1(alu_8bit_1_negative), .in2(alu_16bit_1_negative), .out(Negative), .sel(N));  // open: in3
endmodule

module ALU_4Bit (
  input  [3:0] Opcode,
  input  [3:0] A,
  input  [3:0] B,
  output [3:0] Result,
  output Zero,
  output Negative,
  output Carry,
  output Overflow
);

  wire au_4bit_1_carry, au_4bit_1_overflow, su_4bit_1_carry;
  wire [3:0] au_4bit_1_result, lu_4bit_1_result, su_4bit_1_result;

  AU_4Bit au_4bit_1 (
    .Opcode(Opcode), .A(A), .B(B), .Result(au_4bit_1_result), .Carry(au_4bit_1_carry),
    .Overflow(au_4bit_1_overflow));
  LU_4Bit lu_4bit_1 (.Opcode(Opcode), .A(A), .B(B), .Result(lu_4bit_1_result));
  SU_4Bit su_4bit_1 (.Opcode(Opcode), .A(A), .Result(su_4bit_1_result), .Carry(su_4bit_1_carry));
  Multiplexer #(.select(4), .width(4)) multiplexer_1 (
    .in0(au_4bit_1_result), .in1(au_4bit_1_result), .in2(lu_4bit_1_result), .in3(lu_4bit_1_result),
    .in4(lu_4bit_1_result), .in5(lu_4bit_1_result), .in6(su_4bit_1_result), .in7(su_4bit_1_result),
    .in8(au_4bit_1_result), .in9(au_4bit_1_result), .out({Negative, Result[2:0]}), .sel(Opcode));  // open: in10, in11, in12, in13, in14, in15
  Multiplexer #(.select(4)) multiplexer_2 (
    .in0(au_4bit_1_carry), .in1(au_4bit_1_carry), .in2(1'b0), .in3(1'b0), .in4(1'b0), .in5(1'b0),
    .in6(su_4bit_1_carry), .in7(su_4bit_1_carry), .in8(au_4bit_1_carry), .in9(au_4bit_1_carry), .out(Carry),
    .sel(Opcode));  // open: in10, in11, in12, in13, in14, in15
  Multiplexer #(.select(4)) multiplexer_3 (
    .in0(au_4bit_1_overflow), .in1(au_4bit_1_overflow), .in2(1'b0), .in3(1'b0), .in4(1'b0), .in5(1'b0),
    .in6(1'b0), .in7(1'b0), .in8(au_4bit_1_overflow), .in9(au_4bit_1_overflow), .out(Overflow), .sel(Opcode));  // open: in10, in11, in12, in13, in14, in15
  nor nor_1 (Zero, Result[0], Result[1], Result[2], Negative);

  assign Result[3] = Negative;
endmodule

module ALU_8Bit (
  input  [3:0] Opcode,
  input  [7:0] A,
  input  [7:0] B,
  output [7:0] Result,
  output Zero,
  output Carry,
  output Negative,
  output Overflow
);

  wire au_8bit_1_carry, au_8bit_1_overflow, su_8bit_1_carry;
  wire [7:0] au_8bit_1_result, lu_8bit_1_result, su_8bit_1_result;

  AU_8Bit au_8bit_1 (
    .Opcode(Opcode), .A(A), .B(B), .Result(au_8bit_1_result), .Carry(au_8bit_1_carry),
    .Overflow(au_8bit_1_overflow));
  LU_8Bit lu_8bit_1 (.Opcode(Opcode), .A(A), .B(B), .Result(lu_8bit_1_result));
  SU_8Bit su_8bit_1 (.Opcode(Opcode), .A(A), .Result(su_8bit_1_result), .Carry(su_8bit_1_carry));
  Multiplexer #(.select(4), .width(8)) multiplexer_1 (
    .in0(au_8bit_1_result), .in1(au_8bit_1_result), .in2(lu_8bit_1_result), .in3(lu_8bit_1_result),
    .in4(lu_8bit_1_result), .in5(lu_8bit_1_result), .in6(su_8bit_1_result), .in7(su_8bit_1_result),
    .in8(au_8bit_1_result), .in9(au_8bit_1_result), .out({Negative, Result[6:0]}), .sel(Opcode));  // open: in10, in11, in12, in13, in14, in15
  Multiplexer #(.select(4)) multiplexer_2 (
    .in0(au_8bit_1_carry), .in1(au_8bit_1_carry), .in2(1'b0), .in3(1'b0), .in4(1'b0), .in5(1'b0),
    .in6(su_8bit_1_carry), .in7(su_8bit_1_carry), .in8(au_8bit_1_carry), .in9(au_8bit_1_carry), .out(Carry),
    .sel(Opcode));  // open: in10, in11, in12, in13, in14, in15
  Multiplexer #(.select(4)) multiplexer_3 (
    .in0(au_8bit_1_overflow), .in1(au_8bit_1_overflow), .in2(1'b0), .in3(1'b0), .in4(1'b0), .in5(1'b0),
    .in6(1'b0), .in7(1'b0), .in8(au_8bit_1_overflow), .in9(au_8bit_1_overflow), .out(Overflow), .sel(Opcode));  // open: in10, in11, in12, in13, in14, in15
  nor nor_1 (Zero, Result[0], Result[1], Result[2], Result[3], Result[4], Result[5], Result[6], Negative);

  assign Result[7] = Negative;
endmodule

module ALU_16Bit (
  input  [3:0] Opcode,
  input  [15:0] A,
  input  [15:0] B,
  output [15:0] Result,
  output Zero,
  output Carry,
  output Negative,
  output Overflow
);

  wire au_16bit_1_carry, au_16bit_1_overflow, su_16bit_1_carry;
  wire [15:0] au_16bit_1_result, lu_16bit_1_result, su_16bit_1_result;

  AU_16Bit au_16bit_1 (
    .Opcode(Opcode), .A(A), .B(B), .Result(au_16bit_1_result), .Carry(au_16bit_1_carry),
    .Overflow(au_16bit_1_overflow));
  LU_16Bit lu_16bit_1 (.A(A), .B(B), .Opcode(Opcode), .Result(lu_16bit_1_result));
  SU_16Bit su_16bit_1 (.Opcode(Opcode), .A(A), .Result(su_16bit_1_result), .Carry(su_16bit_1_carry));
  Multiplexer #(.select(4), .width(16)) multiplexer_1 (
    .in0(au_16bit_1_result), .in1(au_16bit_1_result), .in2(lu_16bit_1_result), .in3(lu_16bit_1_result),
    .in4(lu_16bit_1_result), .in5(lu_16bit_1_result), .in6(su_16bit_1_result), .in7(su_16bit_1_result),
    .in8(au_16bit_1_result), .in9(au_16bit_1_result), .out({Negative, Result[14:0]}), .sel(Opcode));  // open: in10, in11, in12, in13, in14, in15
  Multiplexer #(.select(4)) multiplexer_2 (
    .in0(au_16bit_1_carry), .in1(au_16bit_1_carry), .in2(1'b0), .in3(1'b0), .in4(1'b0), .in5(1'b0),
    .in6(su_16bit_1_carry), .in7(su_16bit_1_carry), .in8(au_16bit_1_carry), .in9(au_16bit_1_carry),
    .out(Carry), .sel(Opcode));  // open: in10, in11, in12, in13, in14, in15
  Multiplexer #(.select(4)) multiplexer_3 (
    .in0(au_16bit_1_overflow), .in1(au_16bit_1_overflow), .in2(1'b0), .in3(1'b0), .in4(1'b0), .in5(1'b0),
    .in6(1'b0), .in7(1'b0), .in8(au_16bit_1_overflow), .in9(au_16bit_1_overflow), .out(Overflow), .sel(Opcode));  // open: in10, in11, in12, in13, in14, in15
  nor nor_1 (Zero, Result[0], Result[1], Result[2], Result[3], Result[4], Result[5], Result[6], Result[7], Result[8], Result[9], Result[10], Result[11], Result[12], Result[13], Result[14], Negative);

  assign Result[15] = Negative;
endmodule

module AU_4Bit (
  input  [3:0] Opcode,
  input  [3:0] A,
  input  [3:0] B,
  output [3:0] Result,
  output Carry,
  output Overflow
);

  wire adder_4bit_1_cout, adder_4bit_1_overflow, dec_4bit_1_bout, dec_4bit_1_overflow, inc_4bit_1_cout,
       inc_4bit_1_overflow, subtractor_4bit_1_bout, subtractor_4bit_1_overflow;
  wire [3:0] adder_4bit_1_s0, dec_4bit_1_b0, inc_4bit_1_b0, subtractor_4bit_1_d0;

  Adder_4Bit adder_4bit_1 (
    .A1(A[1]), .B1(B[1]), .A2(A[2]), .B2(B[2]), .A3(A[3]), .B3(B[3]), .A0(A[0]), .B0(B[0]), .Cin(1'b0),
    .S0(adder_4bit_1_s0[0]), .S1(adder_4bit_1_s0[1]), .S2(adder_4bit_1_s0[2]), .S3(adder_4bit_1_s0[3]),
    .Cout(adder_4bit_1_cout), .Overflow(adder_4bit_1_overflow));
  Subtractor_4Bit subtractor_4bit_1 (
    .A1(A[1]), .B1(B[1]), .B2(B[2]), .A2(A[2]), .B3(B[3]), .A3(A[3]), .A0(A[0]), .B0(B[0]),
    .D0(subtractor_4bit_1_d0[0]), .D1(subtractor_4bit_1_d0[1]), .D2(subtractor_4bit_1_d0[2]),
    .D3(subtractor_4bit_1_d0[3]), .Bout(subtractor_4bit_1_bout), .Overflow(subtractor_4bit_1_overflow));
  Inc_4Bit inc_4bit_1 (
    .A0(A[0]), .A1(A[1]), .A2(A[2]), .A3(A[3]), .B0(inc_4bit_1_b0[0]), .B1(inc_4bit_1_b0[1]),
    .B2(inc_4bit_1_b0[2]), .B3(inc_4bit_1_b0[3]), .Cout(inc_4bit_1_cout), .Overflow(inc_4bit_1_overflow));
  Dec_4Bit dec_4bit_1 (
    .A0(A[0]), .A1(A[1]), .A2(A[2]), .A3(A[3]), .B0(dec_4bit_1_b0[0]), .B1(dec_4bit_1_b0[1]),
    .B2(dec_4bit_1_b0[2]), .B3(dec_4bit_1_b0[3]), .Bout(dec_4bit_1_bout), .Overflow(dec_4bit_1_overflow));
  Multiplexer #(.select(4), .width(4)) multiplexer_1 (
    .in0(adder_4bit_1_s0), .in1(subtractor_4bit_1_d0), .in8(inc_4bit_1_b0), .in9(dec_4bit_1_b0),
    .out(Result), .sel(Opcode));  // open: in2, in3, in4, in5, in6, in7, in10, in11, in12, in13, in14, in15
  Multiplexer #(.select(4)) multiplexer_2 (
    .in0(adder_4bit_1_cout), .in1(subtractor_4bit_1_bout), .in8(inc_4bit_1_cout), .in9(dec_4bit_1_bout),
    .out(Carry), .sel(Opcode));  // open: in2, in3, in4, in5, in6, in7, in10, in11, in12, in13, in14, in15
  Multiplexer #(.select(4)) multiplexer_3 (
    .in0(adder_4bit_1_overflow), .in1(subtractor_4bit_1_overflow), .in8(inc_4bit_1_overflow),
    .in9(dec_4bit_1_overflow), .out(Overflow), .sel(Opcode));  // open: in2, in3, in4, in5, in6, in7, in10, in11, in12, in13, in14, in15
endmodule

module AU_8Bit (
  input  [7:0] A,
  input  [3:0] Opcode,
  input  [7:0] B,
  output [7:0] Result,
  output Carry,
  output Overflow
);

  wire adder_8bit_1_cout, adder_8bit_1_overflow, dec_8bit_1_bout, dec_8bit_1_overflow, inc_8bit_1_cout,
       inc_8bit_1_overflow, subtractor_8bit_1_bout, subtractor_8bit_1_overflow;
  wire [7:0] adder_8bit_1_s0, dec_8bit_1_b0, inc_8bit_1_s0, subtractor_8bit_1_d0;

  Adder_8Bit adder_8bit_1 (
    .A4(A[4]), .A5(A[5]), .A6(A[6]), .A7(A[7]), .B4(B[4]), .B5(B[5]), .B6(B[6]), .B7(B[7]), .A0(A[0]),
    .A1(A[1]), .A2(A[2]), .A3(A[3]), .B0(B[0]), .B1(B[1]), .B2(B[2]), .B3(B[3]), .Cin(1'b0),
    .S0(adder_8bit_1_s0[0]), .S1(adder_8bit_1_s0[1]), .S2(adder_8bit_1_s0[2]), .S3(adder_8bit_1_s0[3]),
    .Overflow(adder_8bit_1_overflow), .Cout(adder_8bit_1_cout), .S4(adder_8bit_1_s0[4]),
    .S5(adder_8bit_1_s0[5]), .S6(adder_8bit_1_s0[6]), .S7(adder_8bit_1_s0[7]));
  Subtractor_8Bit subtractor_8bit_1 (
    .B2(B[2]), .B6(B[6]), .A2(A[2]), .A6(A[6]), .B3(B[3]), .B7(B[7]), .A3(A[3]), .A7(A[7]), .A0(A[0]),
    .B0(B[0]), .A4(A[4]), .B4(B[4]), .A1(A[1]), .B1(B[1]), .A5(A[5]), .B5(B[5]),
    .D1(subtractor_8bit_1_d0[1]), .D5(subtractor_8bit_1_d0[5]), .D2(subtractor_8bit_1_d0[2]),
    .D6(subtractor_8bit_1_d0[6]), .D3(subtractor_8bit_1_d0[3]), .D7(subtractor_8bit_1_d0[7]),
    .Bout(subtractor_8bit_1_bout), .Overflow(subtractor_8bit_1_overflow), .D0(subtractor_8bit_1_d0[0]),
    .D4(subtractor_8bit_1_d0[4]));
  Inc_8Bit inc_8bit_1 (
    .A0(A[0]), .A1(A[1]), .A2(A[2]), .A3(A[3]), .A4(A[4]), .A5(A[5]), .A6(A[6]), .A7(A[7]),
    .S0(inc_8bit_1_s0[0]), .S1(inc_8bit_1_s0[1]), .S2(inc_8bit_1_s0[2]), .S3(inc_8bit_1_s0[3]),
    .S4(inc_8bit_1_s0[4]), .S5(inc_8bit_1_s0[5]), .S6(inc_8bit_1_s0[6]), .S7(inc_8bit_1_s0[7]),
    .Cout(inc_8bit_1_cout), .Overflow(inc_8bit_1_overflow));
  Dec_8Bit dec_8bit_1 (
    .A0(A[0]), .A1(A[1]), .A2(A[2]), .A3(A[3]), .A4(A[4]), .A5(A[5]), .A6(A[6]), .A7(A[7]),
    .B0(dec_8bit_1_b0[0]), .B1(dec_8bit_1_b0[1]), .B2(dec_8bit_1_b0[2]), .B3(dec_8bit_1_b0[3]),
    .B4(dec_8bit_1_b0[4]), .B5(dec_8bit_1_b0[5]), .B6(dec_8bit_1_b0[6]), .B7(dec_8bit_1_b0[7]),
    .Bout(dec_8bit_1_bout), .Overflow(dec_8bit_1_overflow));
  Multiplexer #(.select(4), .width(8)) multiplexer_1 (
    .in0(adder_8bit_1_s0), .in1(subtractor_8bit_1_d0), .in8(inc_8bit_1_s0), .in9(dec_8bit_1_b0),
    .out(Result), .sel(Opcode));  // open: in2, in3, in4, in5, in6, in7, in10, in11, in12, in13, in14, in15
  Multiplexer #(.select(4)) multiplexer_2 (
    .in0(adder_8bit_1_cout), .in1(subtractor_8bit_1_bout), .in8(inc_8bit_1_cout), .in9(dec_8bit_1_bout),
    .out(Carry), .sel(Opcode));  // open: in2, in3, in4, in5, in6, in7, in10, in11, in12, in13, in14, in15
  Multiplexer #(.select(4)) multiplexer_3 (
    .in0(adder_8bit_1_overflow), .in1(subtractor_8bit_1_overflow), .in8(inc_8bit_1_overflow),
    .in9(dec_8bit_1_overflow), .out(Overflow), .sel(Opcode));  // open: in2, in3, in4, in5, in6, in7, in10, in11, in12, in13, in14, in15
endmodule

module AU_16Bit (
  input  [15:0] A,
  input  [15:0] B,
  input  [3:0] Opcode,
  output [15:0] Result,
  output Carry,
  output Overflow
);

  wire adder_16bit_1_cout, adder_16bit_1_overflow, dec_16bit_1_bout, dec_16bit_1_overflow, inc_16bit_1_cout,
       inc_16bit_1_overflow, subtractor_16bit_1_bout, subtractor_16bit_1_overflow;
  wire [15:0] adder_16bit_1_s0, dec_16bit_1_d0, inc_16bit_1_s0, subtractor_16bit_1_d0;

  Adder_16Bit adder_16bit_1 (
    .B8(B[8]), .B9(B[9]), .B10(B[10]), .B11(B[11]), .B12(B[12]), .B13(B[13]), .B14(B[14]), .B15(B[15]),
    .A8(A[8]), .A9(A[9]), .A10(A[10]), .A11(A[11]), .A12(A[12]), .A13(A[13]), .A14(A[14]), .A15(A[15]),
    .Cin(1'b0), .B0(B[0]), .B1(B[1]), .B2(B[2]), .B3(B[3]), .B4(B[4]), .B5(B[5]), .B6(B[6]), .B7(B[7]),
    .A0(A[0]), .A1(A[1]), .A2(A[2]), .A3(A[3]), .A4(A[4]), .A5(A[5]), .A6(A[6]), .A7(A[7]),
    .Overflow(adder_16bit_1_overflow), .S8(adder_16bit_1_s0[8]), .S9(adder_16bit_1_s0[9]),
    .S10(adder_16bit_1_s0[10]), .S11(adder_16bit_1_s0[11]), .S12(adder_16bit_1_s0[12]),
    .S13(adder_16bit_1_s0[13]), .S14(adder_16bit_1_s0[14]), .S15(adder_16bit_1_s0[15]),
    .Cout(adder_16bit_1_cout), .S0(adder_16bit_1_s0[0]), .S1(adder_16bit_1_s0[1]), .S2(adder_16bit_1_s0[2]),
    .S3(adder_16bit_1_s0[3]), .S4(adder_16bit_1_s0[4]), .S5(adder_16bit_1_s0[5]), .S6(adder_16bit_1_s0[6]),
    .S7(adder_16bit_1_s0[7]));
  Subtractor_16Bit subtractor_16bit_1 (
    .B10(B[10]), .B14(B[14]), .B2(B[2]), .B6(B[6]), .A10(A[10]), .A14(A[14]), .A2(A[2]), .A6(A[6]),
    .B3(B[3]), .B7(B[7]), .B11(B[11]), .A3(A[3]), .A7(A[7]), .B15(B[15]), .A11(A[11]), .A15(A[15]),
    .B8(B[8]), .A8(A[8]), .A12(A[12]), .B12(B[12]), .A0(A[0]), .B0(B[0]), .A4(A[4]), .B4(B[4]), .B9(B[9]),
    .A9(A[9]), .A13(A[13]), .B13(B[13]), .A1(A[1]), .B1(B[1]), .A5(A[5]), .B5(B[5]),
    .D9(subtractor_16bit_1_d0[9]), .D13(subtractor_16bit_1_d0[13]), .D1(subtractor_16bit_1_d0[1]),
    .D5(subtractor_16bit_1_d0[5]), .D10(subtractor_16bit_1_d0[10]), .D14(subtractor_16bit_1_d0[14]),
    .D2(subtractor_16bit_1_d0[2]), .D6(subtractor_16bit_1_d0[6]), .D3(subtractor_16bit_1_d0[3]),
    .D7(subtractor_16bit_1_d0[7]), .D11(subtractor_16bit_1_d0[11]), .D15(subtractor_16bit_1_d0[15]),
    .Bout(subtractor_16bit_1_bout), .Overflow(subtractor_16bit_1_overflow), .D8(subtractor_16bit_1_d0[8]),
    .D12(subtractor_16bit_1_d0[12]), .D0(subtractor_16bit_1_d0[0]), .D4(subtractor_16bit_1_d0[4]));
  Inc_16Bit inc_16bit_1 (
    .A0(A[0]), .A1(A[1]), .A2(A[2]), .A3(A[3]), .A4(A[4]), .A5(A[5]), .A6(A[6]), .A7(A[7]), .A8(A[8]),
    .A9(A[9]), .A10(A[10]), .A11(A[11]), .A12(A[12]), .A13(A[13]), .A14(A[14]), .A15(A[15]),
    .S0(inc_16bit_1_s0[0]), .S1(inc_16bit_1_s0[1]), .S2(inc_16bit_1_s0[2]), .S3(inc_16bit_1_s0[3]),
    .S4(inc_16bit_1_s0[4]), .S5(inc_16bit_1_s0[5]), .S6(inc_16bit_1_s0[6]), .S7(inc_16bit_1_s0[7]),
    .S8(inc_16bit_1_s0[8]), .S9(inc_16bit_1_s0[9]), .S10(inc_16bit_1_s0[10]), .S11(inc_16bit_1_s0[11]),
    .S12(inc_16bit_1_s0[12]), .S13(inc_16bit_1_s0[13]), .S14(inc_16bit_1_s0[14]), .S15(inc_16bit_1_s0[15]),
    .Cout(inc_16bit_1_cout), .Overflow(inc_16bit_1_overflow));
  Dec_16Bit dec_16bit_1 (
    .A0(A[0]), .A1(A[1]), .A2(A[2]), .A3(A[3]), .A4(A[4]), .A5(A[5]), .A6(A[6]), .A7(A[7]), .A8(A[8]),
    .A9(A[9]), .A10(A[10]), .A11(A[11]), .A12(A[12]), .A13(A[13]), .A14(A[14]), .A15(A[15]),
    .D0(dec_16bit_1_d0[0]), .D1(dec_16bit_1_d0[1]), .D2(dec_16bit_1_d0[2]), .D3(dec_16bit_1_d0[3]),
    .D4(dec_16bit_1_d0[4]), .D5(dec_16bit_1_d0[5]), .D6(dec_16bit_1_d0[6]), .D7(dec_16bit_1_d0[7]),
    .D8(dec_16bit_1_d0[8]), .D9(dec_16bit_1_d0[9]), .D10(dec_16bit_1_d0[10]), .D11(dec_16bit_1_d0[11]),
    .D12(dec_16bit_1_d0[12]), .D13(dec_16bit_1_d0[13]), .D14(dec_16bit_1_d0[14]), .D15(dec_16bit_1_d0[15]),
    .Bout(dec_16bit_1_bout), .Overflow(dec_16bit_1_overflow));
  Multiplexer #(.select(4), .width(16)) multiplexer_1 (
    .in0(adder_16bit_1_s0), .in1(subtractor_16bit_1_d0), .in8(inc_16bit_1_s0), .in9(dec_16bit_1_d0),
    .out(Result), .sel(Opcode));  // open: in2, in3, in4, in5, in6, in7, in10, in11, in12, in13, in14, in15
  Multiplexer #(.select(4)) multiplexer_2 (
    .in0(adder_16bit_1_cout), .in1(subtractor_16bit_1_bout), .in8(inc_16bit_1_cout), .in9(dec_16bit_1_bout),
    .out(Carry), .sel(Opcode));  // open: in2, in3, in4, in5, in6, in7, in10, in11, in12, in13, in14, in15
  Multiplexer #(.select(4)) multiplexer_3 (
    .in0(adder_16bit_1_overflow), .in1(subtractor_16bit_1_overflow), .in8(inc_16bit_1_overflow),
    .in9(dec_16bit_1_overflow), .out(Overflow), .sel(Opcode));  // open: in2, in3, in4, in5, in6, in7, in10, in11, in12, in13, in14, in15
endmodule

module LU_4Bit (
  input  [3:0] Opcode,
  input  [3:0] A,
  input  [3:0] B,
  output [3:0] Result
);

  wire [3:0] and_4bit_1_c0, not_4bit_1_b0, or_4bit_1_c0, xor_4bit_1_c0;

  And_4Bit and_4bit_1 (
    .A0(A[0]), .B0(B[0]), .A1(A[1]), .B1(B[1]), .A2(A[2]), .B2(B[2]), .B3(B[3]), .A3(A[3]),
    .C0(and_4bit_1_c0[0]), .C1(and_4bit_1_c0[1]), .C2(and_4bit_1_c0[2]), .C3(and_4bit_1_c0[3]));
  OR_4Bit or_4bit_1 (
    .A0(A[0]), .B0(B[0]), .A1(A[1]), .B1(B[1]), .A2(A[2]), .B2(B[2]), .B3(B[3]), .A3(A[3]),
    .C0(or_4bit_1_c0[0]), .C1(or_4bit_1_c0[1]), .C2(or_4bit_1_c0[2]), .C3(or_4bit_1_c0[3]));
  XOR_4Bit xor_4bit_1 (
    .A0(A[0]), .B0(B[0]), .A1(A[1]), .B1(B[1]), .A2(A[2]), .B2(B[2]), .B3(B[3]), .A3(A[3]),
    .C0(xor_4bit_1_c0[0]), .C1(xor_4bit_1_c0[1]), .C2(xor_4bit_1_c0[2]), .C3(xor_4bit_1_c0[3]));
  Not_4Bit not_4bit_1 (
    .A0(A[0]), .A1(A[1]), .A2(A[2]), .A3(A[3]), .B0(not_4bit_1_b0[0]), .B1(not_4bit_1_b0[1]),
    .B2(not_4bit_1_b0[2]), .B3(not_4bit_1_b0[3]));
  Multiplexer #(.select(4), .width(4)) multiplexer_1 (
    .in2(and_4bit_1_c0), .in3(or_4bit_1_c0), .in4(xor_4bit_1_c0), .in5(not_4bit_1_b0), .out(Result),
    .sel(Opcode));  // open: in0, in1, in6, in7, in8, in9, in10, in11, in12, in13, in14, in15
endmodule

module LU_8Bit (
  input  [3:0] Opcode,
  input  [7:0] A,
  input  [7:0] B,
  output [7:0] Result
);

  wire [7:0] and_8bit_1_c0, not_8bit_1_b0, or_8bit_1_c0, xor_8bit_1_c0;

  And_8Bit and_8bit_1 (
    .A4(A[4]), .B4(B[4]), .A5(A[5]), .B5(B[5]), .A6(A[6]), .B6(B[6]), .A7(A[7]), .B7(B[7]), .A0(A[0]),
    .B0(B[0]), .A1(A[1]), .B1(B[1]), .A2(A[2]), .B2(B[2]), .B3(B[3]), .A3(A[3]), .C4(and_8bit_1_c0[4]),
    .C5(and_8bit_1_c0[5]), .C6(and_8bit_1_c0[6]), .C7(and_8bit_1_c0[7]), .C0(and_8bit_1_c0[0]),
    .C1(and_8bit_1_c0[1]), .C2(and_8bit_1_c0[2]), .C3(and_8bit_1_c0[3]));
  Or_8Bit or_8bit_1 (
    .A0(A[0]), .B0(B[0]), .A1(A[1]), .B1(B[1]), .A2(A[2]), .B2(B[2]), .B3(B[3]), .A3(A[3]), .A4(A[4]),
    .B4(B[4]), .A5(A[5]), .B5(B[5]), .A6(A[6]), .B6(B[6]), .A7(A[7]), .B7(B[7]), .C0(or_8bit_1_c0[0]),
    .C1(or_8bit_1_c0[1]), .C2(or_8bit_1_c0[2]), .C3(or_8bit_1_c0[3]), .C4(or_8bit_1_c0[4]),
    .C5(or_8bit_1_c0[5]), .C6(or_8bit_1_c0[6]), .C7(or_8bit_1_c0[7]));
  XOR_8Bit xor_8bit_1 (
    .A0(A[0]), .B0(B[0]), .A1(A[1]), .B1(B[1]), .A2(A[2]), .B2(B[2]), .B3(B[3]), .A3(A[3]), .A4(A[4]),
    .B4(B[4]), .A5(A[5]), .B5(B[5]), .A6(A[6]), .B6(B[6]), .A7(A[7]), .B7(B[7]), .C0(xor_8bit_1_c0[0]),
    .C1(xor_8bit_1_c0[1]), .C2(xor_8bit_1_c0[2]), .C3(xor_8bit_1_c0[3]), .C4(xor_8bit_1_c0[4]),
    .C5(xor_8bit_1_c0[5]), .C6(xor_8bit_1_c0[6]), .C7(xor_8bit_1_c0[7]));
  Not_8Bit not_8bit_1 (
    .A0(A[0]), .A1(A[1]), .A2(A[2]), .A3(A[3]), .A4(A[4]), .A5(A[5]), .A6(A[6]), .A7(A[7]),
    .B0(not_8bit_1_b0[0]), .B1(not_8bit_1_b0[1]), .B2(not_8bit_1_b0[2]), .B3(not_8bit_1_b0[3]),
    .B4(not_8bit_1_b0[4]), .B5(not_8bit_1_b0[5]), .B6(not_8bit_1_b0[6]), .B7(not_8bit_1_b0[7]));
  Multiplexer #(.select(4), .width(8)) multiplexer_1 (
    .in2(and_8bit_1_c0), .in3(or_8bit_1_c0), .in4(xor_8bit_1_c0), .in5(not_8bit_1_b0), .out(Result),
    .sel(Opcode));  // open: in0, in1, in6, in7, in8, in9, in10, in11, in12, in13, in14, in15
endmodule

module LU_16Bit (
  input  [15:0] A,
  input  [15:0] B,
  input  [3:0] Opcode,
  output [15:0] Result
);

  wire [15:0] and_16bit_1_c0, not_16bit_1_b0, or_16bit_1_c0, xor_16bit_1_c0;

  And_16Bit and_16bit_1 (
    .A4(A[4]), .B4(B[4]), .A5(A[5]), .B5(B[5]), .A6(A[6]), .B6(B[6]), .A7(A[7]), .B7(B[7]), .A12(A[12]),
    .B12(B[12]), .A13(A[13]), .B13(B[13]), .A14(A[14]), .B14(B[14]), .A15(A[15]), .B15(B[15]), .A0(A[0]),
    .B0(B[0]), .A1(A[1]), .B1(B[1]), .A2(A[2]), .B2(B[2]), .B3(B[3]), .A3(A[3]), .A8(A[8]), .B8(B[8]),
    .A9(A[9]), .B9(B[9]), .A10(A[10]), .B10(B[10]), .A11(A[11]), .B11(B[11]), .C4(and_16bit_1_c0[4]),
    .C5(and_16bit_1_c0[5]), .C6(and_16bit_1_c0[6]), .C7(and_16bit_1_c0[7]), .C12(and_16bit_1_c0[12]),
    .C13(and_16bit_1_c0[13]), .C14(and_16bit_1_c0[14]), .C15(and_16bit_1_c0[15]), .C0(and_16bit_1_c0[0]),
    .C1(and_16bit_1_c0[1]), .C2(and_16bit_1_c0[2]), .C3(and_16bit_1_c0[3]), .C8(and_16bit_1_c0[8]),
    .C9(and_16bit_1_c0[9]), .C10(and_16bit_1_c0[10]), .C11(and_16bit_1_c0[11]));
  Or_16Bit or_16bit_1 (
    .A10(A[10]), .B10(B[10]), .A11(A[11]), .B11(B[11]), .A0(A[0]), .B0(B[0]), .A1(A[1]), .B1(B[1]),
    .A2(A[2]), .B2(B[2]), .B3(B[3]), .A3(A[3]), .A8(A[8]), .B8(B[8]), .A9(A[9]), .B9(B[9]), .B13(B[13]),
    .A14(A[14]), .B14(B[14]), .A15(A[15]), .B15(B[15]), .A4(A[4]), .B4(B[4]), .A5(A[5]), .B5(B[5]),
    .A6(A[6]), .B6(B[6]), .A7(A[7]), .B7(B[7]), .A12(A[12]), .B12(B[12]), .A13(A[13]),
    .C10(or_16bit_1_c0[10]), .C11(or_16bit_1_c0[11]), .C0(or_16bit_1_c0[0]), .C1(or_16bit_1_c0[1]),
    .C2(or_16bit_1_c0[2]), .C3(or_16bit_1_c0[3]), .C8(or_16bit_1_c0[8]), .C9(or_16bit_1_c0[9]),
    .C14(or_16bit_1_c0[14]), .C15(or_16bit_1_c0[15]), .C4(or_16bit_1_c0[4]), .C5(or_16bit_1_c0[5]),
    .C6(or_16bit_1_c0[6]), .C7(or_16bit_1_c0[7]), .C12(or_16bit_1_c0[12]), .C13(or_16bit_1_c0[13]));
  XOR_16Bit xor_16bit_1 (
    .B4(B[4]), .B5(B[5]), .B6(B[6]), .B7(B[7]), .B12(B[12]), .B13(B[13]), .B14(B[14]), .B15(B[15]),
    .A4(A[4]), .A5(A[5]), .A6(A[6]), .A7(A[7]), .A12(A[12]), .A13(A[13]), .A14(A[14]), .A15(A[15]),
    .B8(B[8]), .B9(B[9]), .B10(B[10]), .B11(B[11]), .B0(B[0]), .B1(B[1]), .B2(B[2]), .B3(B[3]), .A8(A[8]),
    .A9(A[9]), .A10(A[10]), .A11(A[11]), .A0(A[0]), .A1(A[1]), .A2(A[2]), .A3(A[3]), .C4(xor_16bit_1_c0[4]),
    .C5(xor_16bit_1_c0[5]), .C6(xor_16bit_1_c0[6]), .C7(xor_16bit_1_c0[7]), .C12(xor_16bit_1_c0[12]),
    .C13(xor_16bit_1_c0[13]), .C14(xor_16bit_1_c0[14]), .C15(xor_16bit_1_c0[15]), .C8(xor_16bit_1_c0[8]),
    .C9(xor_16bit_1_c0[9]), .C10(xor_16bit_1_c0[10]), .C11(xor_16bit_1_c0[11]), .C0(xor_16bit_1_c0[0]),
    .C1(xor_16bit_1_c0[1]), .C2(xor_16bit_1_c0[2]), .C3(xor_16bit_1_c0[3]));
  Not_16Bit not_16bit_1 (
    .A0(A[0]), .A1(A[1]), .A2(A[2]), .A3(A[3]), .A4(A[4]), .A5(A[5]), .A6(A[6]), .A7(A[7]), .A8(A[8]),
    .A9(A[9]), .A10(A[10]), .A11(A[11]), .A12(A[12]), .A13(A[13]), .A14(A[14]), .A15(A[15]),
    .B0(not_16bit_1_b0[0]), .B1(not_16bit_1_b0[1]), .B2(not_16bit_1_b0[2]), .B3(not_16bit_1_b0[3]),
    .B4(not_16bit_1_b0[4]), .B5(not_16bit_1_b0[5]), .B6(not_16bit_1_b0[6]), .B7(not_16bit_1_b0[7]),
    .B8(not_16bit_1_b0[8]), .B9(not_16bit_1_b0[9]), .B10(not_16bit_1_b0[10]), .B11(not_16bit_1_b0[11]),
    .B12(not_16bit_1_b0[12]), .B13(not_16bit_1_b0[13]), .B14(not_16bit_1_b0[14]), .B15(not_16bit_1_b0[15]));
  Multiplexer #(.select(4), .width(16)) multiplexer_1 (
    .in2(and_16bit_1_c0), .in3(or_16bit_1_c0), .in4(xor_16bit_1_c0), .in5(not_16bit_1_b0), .out(Result),
    .sel(Opcode));  // open: in0, in1, in6, in7, in8, in9, in10, in11, in12, in13, in14, in15
endmodule

module SU_4Bit (
  input  [3:0] Opcode,
  input  [3:0] A,
  output [3:0] Result,
  output Carry
);

  wire shl_4bit_1_carry, shr_4bit_1_carry;
  wire [3:0] shl_4bit_1_result, shr_4bit_1_result;

  SHL_4Bit shl_4bit_1 (.A(A), .Result(shl_4bit_1_result), .Carry(shl_4bit_1_carry));
  SHR_4Bit shr_4bit_1 (.A(A), .Carry(shr_4bit_1_carry), .Result(shr_4bit_1_result));
  Multiplexer #(.select(4), .width(4)) multiplexer_1 (
    .in6(shl_4bit_1_result), .in7(shr_4bit_1_result), .out(Result), .sel(Opcode));  // open: in0, in1, in2, in3, in4, in5, in8, in9, in10, in11, in12, in13, in14, in15
  Multiplexer #(.select(4)) multiplexer_2 (
    .in6(shl_4bit_1_carry), .in7(shr_4bit_1_carry), .out(Carry), .sel(Opcode));  // open: in0, in1, in2, in3, in4, in5, in8, in9, in10, in11, in12, in13, in14, in15
endmodule

module SU_8Bit (
  input  [3:0] Opcode,
  input  [7:0] A,
  output [7:0] Result,
  output Carry
);

  wire shl_8bit_1_carry, shr_8bit_1_carry;
  wire [7:0] shl_8bit_1_result, shr_8bit_1_result;

  SHL_8Bit shl_8bit_1 (.A(A), .Result(shl_8bit_1_result), .Carry(shl_8bit_1_carry));
  SHR_8Bit shr_8bit_1 (.A(A), .Carry(shr_8bit_1_carry), .Result(shr_8bit_1_result));
  Multiplexer #(.select(4), .width(8)) multiplexer_1 (
    .in6(shl_8bit_1_result), .in7(shr_8bit_1_result), .out(Result), .sel(Opcode));  // open: in0, in1, in2, in3, in4, in5, in8, in9, in10, in11, in12, in13, in14, in15
  Multiplexer #(.select(4)) multiplexer_2 (
    .in6(shl_8bit_1_carry), .in7(shr_8bit_1_carry), .out(Carry), .sel(Opcode));  // open: in0, in1, in2, in3, in4, in5, in8, in9, in10, in11, in12, in13, in14, in15
endmodule

module SU_16Bit (
  input  [3:0] Opcode,
  input  [15:0] A,
  output [15:0] Result,
  output Carry
);

  wire shl_16bit_1_carry, shr_16bit_1_carry;
  wire [15:0] shl_16bit_1_result, shr_16bit_1_result;

  SHL_16Bit shl_16bit_1 (.A(A), .Result(shl_16bit_1_result), .Carry(shl_16bit_1_carry));
  SHR_16Bit shr_16bit_1 (.A(A), .Carry(shr_16bit_1_carry), .Result(shr_16bit_1_result));
  Multiplexer #(.select(4), .width(16)) multiplexer_1 (
    .in6(shl_16bit_1_result), .in7(shr_16bit_1_result), .out(Result), .sel(Opcode));  // open: in0, in1, in2, in3, in4, in5, in8, in9, in10, in11, in12, in13, in14, in15
  Multiplexer #(.select(4)) multiplexer_2 (
    .in6(shl_16bit_1_carry), .in7(shr_16bit_1_carry), .out(Carry), .sel(Opcode));  // open: in0, in1, in2, in3, in4, in5, in8, in9, in10, in11, in12, in13, in14, in15
endmodule

module Adder_4Bit (
  input  A0,
  input  A1,
  input  A2,
  input  A3,
  input  B1,
  input  B2,
  input  B3,
  input  B0,
  input  Cin,
  output S0,
  output S1,
  output S2,
  output S3,
  output Cout,
  output Overflow
);

  wire Adder1_cout, Adder2_cout, full_adder_1_cout;

  Full_Adder Adder1 (.A(A0), .B(B0), .Cin(Cin), .S(S0), .Cout(Adder1_cout));
  Full_Adder Adder2 (.A(A1), .B(B1), .Cin(Adder1_cout), .S(S1), .Cout(Adder2_cout));
  Full_Adder full_adder_1 (.A(A2), .B(B2), .Cin(Adder2_cout), .S(S2), .Cout(full_adder_1_cout));
  Full_Adder full_adder_2 (.A(A3), .B(B3), .Cin(full_adder_1_cout), .S(S3), .Cout(Cout));
  xor xor_1 (Overflow, Cout, full_adder_1_cout);
endmodule

module Adder_8Bit (
  input  A0,
  input  A4,
  input  A1,
  input  A5,
  input  A2,
  input  A6,
  input  A3,
  input  A7,
  input  B0,
  input  B4,
  input  B1,
  input  B5,
  input  B2,
  input  B6,
  input  B3,
  input  B7,
  input  Cin,
  output S0,
  output S4,
  output S1,
  output S5,
  output S2,
  output S6,
  output S3,
  output S7,
  output Cout,
  output Overflow
);

  wire adder_4bit_1_cout;

  Adder_4Bit adder_4bit_1 (
    .A1(A1), .B1(B1), .A2(A2), .B2(B2), .A3(A3), .B3(B3), .A0(A0), .B0(B0), .Cin(Cin), .S0(S0), .S1(S1),
    .S2(S2), .S3(S3), .Cout(adder_4bit_1_cout));  // open: Overflow
  Adder_4Bit adder_4bit_2 (
    .A1(A5), .B1(B5), .A2(A6), .B2(B6), .A3(A7), .B3(B7), .A0(A4), .B0(B4), .Cin(adder_4bit_1_cout), .S0(S4),
    .S1(S5), .S2(S6), .S3(S7), .Cout(Cout), .Overflow(Overflow));
endmodule

module Adder_16Bit (
  input  B8,
  input  A8,
  input  B0,
  input  A0,
  input  B9,
  input  A9,
  input  B1,
  input  A1,
  input  B10,
  input  A10,
  input  B2,
  input  A2,
  input  B11,
  input  A11,
  input  B3,
  input  A3,
  input  B12,
  input  A12,
  input  B4,
  input  A4,
  input  B13,
  input  A13,
  input  B5,
  input  A5,
  input  B14,
  input  A14,
  input  B6,
  input  A6,
  input  B15,
  input  A15,
  input  B7,
  input  A7,
  input  Cin,
  output S8,
  output S0,
  output S9,
  output S1,
  output S10,
  output S2,
  output S11,
  output S3,
  output S12,
  output S4,
  output S13,
  output S5,
  output S14,
  output S6,
  output S15,
  output S7,
  output Cout,
  output Overflow
);

  wire adder_8bit_1_overflow;

  Adder_8Bit adder_8bit_1 (
    .A4(A4), .A5(A5), .A6(A6), .A7(A7), .B4(B4), .B5(B5), .B6(B6), .B7(B7), .A0(A0), .A1(A1), .A2(A2),
    .A3(A3), .B0(B0), .B1(B1), .B2(B2), .B3(B3), .Cin(Cin), .S0(S0), .S1(S1), .S2(S2), .S3(S3),
    .Overflow(adder_8bit_1_overflow), .Cout(adder_8bit_1_overflow), .S4(S4), .S5(S5), .S6(S6), .S7(S7));
  Adder_8Bit adder_8bit_2 (
    .A4(A12), .A5(A13), .A6(A14), .A7(A15), .B4(B12), .B5(B13), .B6(B14), .B7(B15), .A0(A8), .A1(A9),
    .A2(A10), .A3(A11), .B0(B8), .B1(B9), .B2(B10), .B3(B11), .Cin(adder_8bit_1_overflow), .S0(S8), .S1(S9),
    .S2(S10), .S3(S11), .Overflow(Overflow), .Cout(Cout), .S4(S12), .S5(S13), .S6(S14), .S7(S15));
endmodule

module Subtractor_4Bit (
  input  A0,
  input  A1,
  input  A2,
  input  A3,
  input  B1,
  input  B0,
  input  B2,
  input  B3,
  output D0,
  output D1,
  output D2,
  output D3,
  output Bout,
  output Overflow
);

  wire Adder1_cout, Adder2_cout, full_adder_1_cout, full_adder_2_cout, not_1_out, not_2_out, not_3_out,
       not_4_out;

  not not_1 (not_1_out, B0);
  Full_Adder Adder1 (.A(A0), .B(not_1_out), .Cin(1'b1), .S(D0), .Cout(Adder1_cout));
  not not_2 (not_2_out, B1);
  Full_Adder Adder2 (.A(A1), .B(not_2_out), .Cin(Adder1_cout), .S(D1), .Cout(Adder2_cout));
  not not_3 (not_3_out, B2);
  Full_Adder full_adder_1 (.A(A2), .B(not_3_out), .Cin(Adder2_cout), .S(D2), .Cout(full_adder_1_cout));
  not not_4 (not_4_out, B3);
  Full_Adder full_adder_2 (.A(A3), .B(not_4_out), .Cin(full_adder_1_cout), .S(D3), .Cout(full_adder_2_cout));
  not not_5 (Bout, full_adder_2_cout);
  xor xor_1 (Overflow, full_adder_2_cout, full_adder_1_cout);
endmodule

module Subtractor_8Bit (
  input  A0,
  input  A1,
  input  A2,
  input  A3,
  input  B1,
  input  B0,
  input  B2,
  input  B3,
  input  A4,
  input  A5,
  input  A6,
  input  A7,
  input  B5,
  input  B4,
  input  B6,
  input  B7,
  output D0,
  output D1,
  output D2,
  output D3,
  output D4,
  output D5,
  output D6,
  output D7,
  output Bout,
  output Overflow
);

  wire Adder1_cout, Adder2_cout, full_adder_1_cout, full_adder_2_cout, full_adder_3_cout, full_adder_4_cout,
       full_adder_5_cout, full_adder_6_cout, not_1_out, not_2_out, not_3_out, not_4_out, not_5_out,
       not_6_out, not_7_out, not_8_out;

  not not_1 (not_1_out, B0);
  not not_2 (not_2_out, B4);
  Full_Adder Adder1 (.A(A0), .B(not_1_out), .Cin(1'b1), .S(D0), .Cout(Adder1_cout));
  Full_Adder full_adder_1 (.A(A4), .B(not_2_out), .Cin(full_adder_5_cout), .S(D4), .Cout(full_adder_1_cout));
  not not_3 (not_3_out, B1);
  not not_4 (not_4_out, B5);
  Full_Adder Adder2 (.A(A1), .B(not_3_out), .Cin(Adder1_cout), .S(D1), .Cout(Adder2_cout));
  Full_Adder full_adder_2 (.A(A5), .B(not_4_out), .Cin(full_adder_1_cout), .S(D5), .Cout(full_adder_2_cout));
  not not_5 (not_5_out, B2);
  not not_6 (not_6_out, B6);
  Full_Adder full_adder_3 (.A(A2), .B(not_5_out), .Cin(Adder2_cout), .S(D2), .Cout(full_adder_3_cout));
  Full_Adder full_adder_4 (.A(A6), .B(not_6_out), .Cin(full_adder_2_cout), .S(D6), .Cout(full_adder_4_cout));
  not not_7 (not_7_out, B3);
  not not_8 (not_8_out, B7);
  Full_Adder full_adder_5 (.A(A3), .B(not_7_out), .Cin(full_adder_3_cout), .S(D3), .Cout(full_adder_5_cout));
  Full_Adder full_adder_6 (.A(A7), .B(not_8_out), .Cin(full_adder_4_cout), .S(D7), .Cout(full_adder_6_cout));
  not not_9 (Bout, full_adder_6_cout);
  xor xor_1 (Overflow, full_adder_6_cout, full_adder_4_cout);
endmodule

module Subtractor_16Bit (
  input  A0,
  input  A1,
  input  A2,
  input  A3,
  input  B1,
  input  B0,
  input  B2,
  input  B3,
  input  A4,
  input  A5,
  input  A6,
  input  A7,
  input  B5,
  input  B4,
  input  B6,
  input  B7,
  input  A8,
  input  A9,
  input  A10,
  input  A11,
  input  B9,
  input  B8,
  input  B10,
  input  B11,
  input  A12,
  input  A13,
  input  A14,
  input  A15,
  input  B13,
  input  B12,
  input  B14,
  input  B15,
  output D0,
  output D1,
  output D2,
  output D3,
  output D4,
  output D5,
  output D6,
  output D7,
  output D8,
  output D9,
  output D10,
  output D11,
  output D12,
  output D13,
  output D14,
  output D15,
  output Bout,
  output Overflow
);

  wire Adder1_cout, Adder2_cout, full_adder_1_cout, full_adder_2_cout, full_adder_3_cout, full_adder_4_cout,
       full_adder_5_cout, full_adder_6_cout, full_adder_7_cout, full_adder_8_cout, full_adder_9_cout,
       full_adder_10_cout, full_adder_11_cout, full_adder_12_cout, full_adder_13_cout, full_adder_14_cout,
       not_1_out, not_2_out, not_3_out, not_4_out, not_5_out, not_6_out, not_7_out, not_8_out, not_9_out,
       not_10_out, not_11_out, not_12_out, not_13_out, not_14_out, not_15_out, not_16_out;

  not not_1 (not_1_out, B0);
  not not_2 (not_2_out, B4);
  not not_3 (not_3_out, B8);
  not not_4 (not_4_out, B12);
  Full_Adder Adder1 (.A(A0), .B(not_1_out), .Cin(1'b1), .S(D0), .Cout(Adder1_cout));
  Full_Adder full_adder_1 (.A(A4), .B(not_2_out), .Cin(full_adder_11_cout), .S(D4), .Cout(full_adder_1_cout));
  Full_Adder full_adder_2 (.A(A8), .B(not_3_out), .Cin(full_adder_12_cout), .S(D8), .Cout(full_adder_2_cout));
  Full_Adder full_adder_3 (.A(A12), .B(not_4_out), .Cin(full_adder_13_cout), .S(D12), .Cout(full_adder_3_cout));
  not not_5 (not_5_out, B1);
  not not_6 (not_6_out, B5);
  not not_7 (not_7_out, B9);
  not not_8 (not_8_out, B13);
  Full_Adder Adder2 (.A(A1), .B(not_5_out), .Cin(Adder1_cout), .S(D1), .Cout(Adder2_cout));
  Full_Adder full_adder_4 (.A(A5), .B(not_6_out), .Cin(full_adder_1_cout), .S(D5), .Cout(full_adder_4_cout));
  Full_Adder full_adder_5 (.A(A9), .B(not_7_out), .Cin(full_adder_2_cout), .S(D9), .Cout(full_adder_5_cout));
  Full_Adder full_adder_6 (.A(A13), .B(not_8_out), .Cin(full_adder_3_cout), .S(D13), .Cout(full_adder_6_cout));
  not not_9 (not_9_out, B2);
  not not_10 (not_10_out, B6);
  not not_11 (not_11_out, B10);
  not not_12 (not_12_out, B14);
  Full_Adder full_adder_7 (.A(A2), .B(not_9_out), .Cin(Adder2_cout), .S(D2), .Cout(full_adder_7_cout));
  Full_Adder full_adder_8 (.A(A6), .B(not_10_out), .Cin(full_adder_4_cout), .S(D6), .Cout(full_adder_8_cout));
  Full_Adder full_adder_9 (.A(A10), .B(not_11_out), .Cin(full_adder_5_cout), .S(D10), .Cout(full_adder_9_cout));
  Full_Adder full_adder_10 (.A(A14), .B(not_12_out), .Cin(full_adder_6_cout), .S(D14), .Cout(full_adder_10_cout));
  not not_13 (not_13_out, B3);
  not not_14 (not_14_out, B7);
  not not_15 (not_15_out, B11);
  not not_16 (not_16_out, B15);
  Full_Adder full_adder_11 (.A(A3), .B(not_13_out), .Cin(full_adder_7_cout), .S(D3), .Cout(full_adder_11_cout));
  Full_Adder full_adder_12 (.A(A7), .B(not_14_out), .Cin(full_adder_8_cout), .S(D7), .Cout(full_adder_12_cout));
  Full_Adder full_adder_13 (.A(A11), .B(not_15_out), .Cin(full_adder_9_cout), .S(D11), .Cout(full_adder_13_cout));
  Full_Adder full_adder_14 (.A(A15), .B(not_16_out), .Cin(full_adder_10_cout), .S(D15), .Cout(full_adder_14_cout));
  not not_17 (Bout, full_adder_14_cout);
  xor xor_1 (Overflow, full_adder_14_cout, full_adder_10_cout);
endmodule

module And_4Bit (
  input  A0,
  input  B0,
  input  A1,
  input  B1,
  input  A2,
  input  B2,
  input  B3,
  input  A3,
  output C0,
  output C1,
  output C2,
  output C3
);

  and and_1 (C0, A0, B0);
  and and_2 (C1, A1, B1);
  and and_3 (C2, A2, B2);
  and and_4 (C3, B3, A3);
endmodule

module And_8Bit (
  input  A0,
  input  A4,
  input  B0,
  input  B4,
  input  A1,
  input  A5,
  input  B1,
  input  B5,
  input  A2,
  input  A6,
  input  B2,
  input  B6,
  input  B3,
  input  A7,
  input  A3,
  input  B7,
  output C0,
  output C4,
  output C1,
  output C5,
  output C2,
  output C6,
  output C3,
  output C7
);

  and and_1 (C0, A0, B0);
  and and_2 (C1, A1, B1);
  and and_3 (C2, A2, B2);
  and and_4 (C3, B3, A3);
  and and_5 (C4, A4, B4);
  and and_6 (C5, A5, B5);
  and and_7 (C6, A6, B6);
  and and_8 (C7, A7, B7);
endmodule

module And_16Bit (
  input  A0,
  input  A4,
  input  B0,
  input  B4,
  input  A1,
  input  A5,
  input  B1,
  input  B5,
  input  A2,
  input  A6,
  input  B2,
  input  B6,
  input  B3,
  input  A7,
  input  A3,
  input  B7,
  input  A8,
  input  A12,
  input  B8,
  input  B12,
  input  A9,
  input  A13,
  input  B9,
  input  B13,
  input  A10,
  input  A14,
  input  B10,
  input  B14,
  input  A11,
  input  A15,
  input  B11,
  input  B15,
  output C0,
  output C4,
  output C1,
  output C5,
  output C2,
  output C6,
  output C3,
  output C7,
  output C8,
  output C12,
  output C9,
  output C13,
  output C10,
  output C14,
  output C11,
  output C15
);

  and and_1 (C0, A0, B0);
  and and_2 (C1, A1, B1);
  and and_3 (C2, A2, B2);
  and and_4 (C3, B3, A3);
  and and_5 (C8, A8, B8);
  and and_6 (C9, A9, B9);
  and and_7 (C10, A10, B10);
  and and_8 (C11, A11, B11);
  and and_9 (C4, A4, B4);
  and and_10 (C5, A5, B5);
  and and_11 (C6, A6, B6);
  and and_12 (C7, A7, B7);
  and and_13 (C12, A12, B12);
  and and_14 (C13, A13, B13);
  and and_15 (C14, A14, B14);
  and and_16 (C15, A15, B15);
endmodule

module OR_4Bit (
  input  A0,
  input  B0,
  input  A1,
  input  B1,
  input  A2,
  input  B2,
  input  B3,
  input  A3,
  output C0,
  output C1,
  output C2,
  output C3
);

  or or_1 (C0, A0, B0);
  or or_2 (C1, A1, B1);
  or or_3 (C2, A2, B2);
  or or_4 (C3, B3, A3);
endmodule

module Or_8Bit (
  input  A0,
  input  A4,
  input  B0,
  input  B4,
  input  A1,
  input  A5,
  input  B1,
  input  B5,
  input  A2,
  input  A6,
  input  B2,
  input  B6,
  input  B3,
  input  A7,
  input  A3,
  input  B7,
  output C0,
  output C4,
  output C1,
  output C5,
  output C2,
  output C6,
  output C3,
  output C7
);

  or or_1 (C0, A0, B0);
  or or_2 (C1, A1, B1);
  or or_3 (C2, A2, B2);
  or or_4 (C3, B3, A3);
  or or_5 (C4, A4, B4);
  or or_6 (C5, A5, B5);
  or or_7 (C6, A6, B6);
  or or_8 (C7, A7, B7);
endmodule

module Or_16Bit (
  input  A0,
  input  A4,
  input  B0,
  input  B4,
  input  A1,
  input  A5,
  input  B1,
  input  B5,
  input  A2,
  input  A6,
  input  B2,
  input  B6,
  input  B3,
  input  A7,
  input  A3,
  input  B7,
  input  A8,
  input  A12,
  input  B8,
  input  B12,
  input  A9,
  input  A13,
  input  B9,
  input  B13,
  input  A10,
  input  A14,
  input  B10,
  input  B14,
  input  A11,
  input  A15,
  input  B11,
  input  B15,
  output C0,
  output C4,
  output C1,
  output C5,
  output C2,
  output C6,
  output C3,
  output C7,
  output C8,
  output C12,
  output C9,
  output C13,
  output C10,
  output C14,
  output C11,
  output C15
);

  or or_1 (C0, A0, B0);
  or or_2 (C1, A1, B1);
  or or_3 (C2, A2, B2);
  or or_4 (C3, B3, A3);
  or or_5 (C8, A8, B8);
  or or_6 (C9, A9, B9);
  or or_7 (C10, A10, B10);
  or or_8 (C11, A11, B11);
  or or_9 (C4, A4, B4);
  or or_10 (C5, A5, B5);
  or or_11 (C6, A6, B6);
  or or_12 (C7, A7, B7);
  or or_13 (C12, A12, B12);
  or or_14 (C13, A13, B13);
  or or_15 (C14, A14, B14);
  or or_16 (C15, A15, B15);
endmodule

module XOR_4Bit (
  input  A0,
  input  B0,
  input  A1,
  input  B1,
  input  A2,
  input  B2,
  input  B3,
  input  A3,
  output C0,
  output C1,
  output C2,
  output C3
);

  xor xor_1 (C0, A0, B0);
  xor xor_2 (C1, A1, B1);
  xor xor_3 (C2, A2, B2);
  xor xor_4 (C3, B3, A3);
endmodule

module XOR_8Bit (
  input  A0,
  input  A4,
  input  B0,
  input  B4,
  input  A1,
  input  A5,
  input  B1,
  input  B5,
  input  A2,
  input  A6,
  input  B2,
  input  B6,
  input  B3,
  input  A7,
  input  A3,
  input  B7,
  output C0,
  output C4,
  output C1,
  output C5,
  output C2,
  output C6,
  output C3,
  output C7
);

  xor xor_1 (C0, A0, B0);
  xor xor_2 (C1, A1, B1);
  xor xor_3 (C2, A2, B2);
  xor xor_4 (C3, B3, A3);
  xor xor_5 (C4, A4, B4);
  xor xor_6 (C5, A5, B5);
  xor xor_7 (C6, A6, B6);
  xor xor_8 (C7, A7, B7);
endmodule

module XOR_16Bit (
  input  A0,
  input  A4,
  input  B0,
  input  B4,
  input  A1,
  input  A5,
  input  B1,
  input  B5,
  input  A2,
  input  A6,
  input  B2,
  input  B6,
  input  A3,
  input  A7,
  input  B3,
  input  B7,
  input  A8,
  input  A12,
  input  B8,
  input  B12,
  input  A9,
  input  A13,
  input  B9,
  input  B13,
  input  A10,
  input  A14,
  input  B10,
  input  B14,
  input  A11,
  input  A15,
  input  B11,
  input  B15,
  output C0,
  output C4,
  output C1,
  output C5,
  output C2,
  output C6,
  output C3,
  output C7,
  output C8,
  output C12,
  output C9,
  output C13,
  output C10,
  output C14,
  output C11,
  output C15
);

  xor xor_1 (C0, A0, B0);
  xor xor_2 (C1, A1, B1);
  xor xor_3 (C2, A2, B2);
  xor xor_4 (C3, A3, B3);
  xor xor_5 (C8, A8, B8);
  xor xor_6 (C9, A9, B9);
  xor xor_7 (C10, A10, B10);
  xor xor_8 (C11, A11, B11);
  xor xor_9 (C4, A4, B4);
  xor xor_10 (C5, A5, B5);
  xor xor_11 (C6, A6, B6);
  xor xor_12 (C7, A7, B7);
  xor xor_13 (C12, A12, B12);
  xor xor_14 (C13, A13, B13);
  xor xor_15 (C14, A14, B14);
  xor xor_16 (C15, A15, B15);
endmodule

module Not_4Bit (
  input  A0,
  input  A1,
  input  A2,
  input  A3,
  output B0,
  output B1,
  output B2,
  output B3
);

  not not_1 (B0, A0);
  not not_2 (B1, A1);
  not not_3 (B2, A2);
  not not_4 (B3, A3);
endmodule

module Not_8Bit (
  input  A0,
  input  A1,
  input  A2,
  input  A3,
  input  A4,
  input  A5,
  input  A6,
  input  A7,
  output B0,
  output B1,
  output B2,
  output B3,
  output B4,
  output B5,
  output B6,
  output B7
);

  not not_1 (B0, A0);
  not not_2 (B1, A1);
  not not_3 (B2, A2);
  not not_4 (B3, A3);
  not not_5 (B4, A4);
  not not_6 (B5, A5);
  not not_7 (B6, A6);
  not not_8 (B7, A7);
endmodule

module Not_16Bit (
  input  A0,
  input  A1,
  input  A2,
  input  A3,
  input  A4,
  input  A5,
  input  A6,
  input  A7,
  input  A8,
  input  A9,
  input  A10,
  input  A11,
  input  A12,
  input  A13,
  input  A14,
  input  A15,
  output B0,
  output B1,
  output B2,
  output B3,
  output B4,
  output B5,
  output B6,
  output B7,
  output B8,
  output B9,
  output B10,
  output B11,
  output B12,
  output B13,
  output B14,
  output B15
);

  not not_1 (B0, A0);
  not not_2 (B1, A1);
  not not_3 (B2, A2);
  not not_4 (B3, A3);
  not not_5 (B4, A4);
  not not_6 (B5, A5);
  not not_7 (B6, A6);
  not not_8 (B7, A7);
  not not_9 (B8, A8);
  not not_10 (B9, A9);
  not not_11 (B10, A10);
  not not_12 (B11, A11);
  not not_13 (B12, A12);
  not not_14 (B13, A13);
  not not_15 (B14, A14);
  not not_16 (B15, A15);
endmodule

module Inc_4Bit (
  input  A0,
  input  A1,
  input  A2,
  input  A3,
  output B0,
  output B1,
  output B2,
  output B3,
  output Cout,
  output Overflow
);

  Adder_4Bit adder_4bit_1 (
    .A1(A1), .B1(1'b0), .A2(A2), .B2(1'b0), .A3(A3), .B3(1'b0), .A0(A0), .B0(1'b1), .Cin(1'b0), .S0(B0),
    .S1(B1), .S2(B2), .S3(B3), .Cout(Cout), .Overflow(Overflow));
endmodule

module Inc_8Bit (
  input  A0,
  input  A1,
  input  A2,
  input  A3,
  input  A4,
  input  A5,
  input  A6,
  input  A7,
  output S0,
  output S1,
  output S2,
  output S3,
  output S4,
  output S5,
  output S6,
  output S7,
  output Cout,
  output Overflow
);

  Adder_8Bit adder_8bit_1 (
    .A4(A4), .A5(A5), .A6(A6), .A7(A7), .B4(1'b0), .B5(1'b0), .B6(1'b0), .B7(1'b0), .A0(A0), .A1(A1),
    .A2(A2), .A3(A3), .B0(1'b1), .B1(1'b0), .B2(1'b0), .B3(1'b0), .Cin(1'b0), .S0(S0), .S1(S1), .S2(S2),
    .S3(S3), .Overflow(Overflow), .Cout(Cout), .S4(S4), .S5(S5), .S6(S6), .S7(S7));
endmodule

module Inc_16Bit (
  input  A0,
  input  A1,
  input  A2,
  input  A3,
  input  A4,
  input  A5,
  input  A6,
  input  A7,
  input  A8,
  input  A9,
  input  A10,
  input  A11,
  input  A12,
  input  A13,
  input  A14,
  input  A15,
  output S0,
  output S1,
  output S2,
  output S3,
  output S4,
  output S5,
  output S6,
  output S7,
  output S8,
  output S9,
  output S10,
  output S11,
  output S12,
  output S13,
  output S14,
  output S15,
  output Cout,
  output Overflow
);

  Adder_16Bit adder_16bit_1 (
    .B8(1'b0), .B9(1'b0), .B10(1'b0), .B11(1'b0), .B12(1'b0), .B13(1'b0), .B14(1'b0), .B15(1'b0), .A8(A8),
    .A9(A9), .A10(A10), .A11(A11), .A12(A12), .A13(A13), .A14(A14), .A15(A15), .Cin(1'b0), .B0(1'b1),
    .B1(1'b0), .B2(1'b0), .B3(1'b0), .B4(1'b0), .B5(1'b0), .B6(1'b0), .B7(1'b0), .A0(A0), .A1(A1), .A2(A2),
    .A3(A3), .A4(A4), .A5(A5), .A6(A6), .A7(A7), .Overflow(Overflow), .S8(S8), .S9(S9), .S10(S10), .S11(S11),
    .S12(S12), .S13(S13), .S14(S14), .S15(S15), .Cout(Cout), .S0(S0), .S1(S1), .S2(S2), .S3(S3), .S4(S4),
    .S5(S5), .S6(S6), .S7(S7));
endmodule

module Dec_4Bit (
  input  A0,
  input  A1,
  input  A2,
  input  A3,
  output B0,
  output B1,
  output B2,
  output B3,
  output Bout,
  output Overflow
);

  Subtractor_4Bit subtractor_4bit_1 (
    .A1(A1), .B1(1'b0), .B2(1'b0), .A2(A2), .B3(1'b0), .A3(A3), .A0(A0), .B0(1'b1), .D0(B0), .D1(B1),
    .D2(B2), .D3(B3), .Bout(Bout), .Overflow(Overflow));
endmodule

module Dec_8Bit (
  input  A0,
  input  A1,
  input  A2,
  input  A3,
  input  A4,
  input  A5,
  input  A6,
  input  A7,
  output B0,
  output B1,
  output B2,
  output B3,
  output B4,
  output B5,
  output B6,
  output B7,
  output Bout,
  output Overflow
);

  Subtractor_8Bit subtractor_8bit_1 (
    .B2(1'b0), .B6(1'b0), .A2(A2), .A6(A6), .B3(1'b0), .B7(1'b0), .A3(A3), .A7(A7), .A0(A0), .B0(1'b1),
    .A4(A4), .B4(1'b0), .A1(A1), .B1(1'b0), .A5(A5), .B5(1'b0), .D1(B1), .D5(B5), .D2(B2), .D6(B6), .D3(B3),
    .D7(B7), .Bout(Bout), .Overflow(Overflow), .D0(B0), .D4(B4));
endmodule

module Dec_16Bit (
  input  A0,
  input  A1,
  input  A2,
  input  A3,
  input  A4,
  input  A5,
  input  A6,
  input  A7,
  input  A8,
  input  A9,
  input  A10,
  input  A11,
  input  A12,
  input  A13,
  input  A14,
  input  A15,
  output D0,
  output D1,
  output D2,
  output D3,
  output D4,
  output D5,
  output D6,
  output D7,
  output D8,
  output D9,
  output D10,
  output D11,
  output D12,
  output D13,
  output D14,
  output D15,
  output Bout,
  output Overflow
);

  Subtractor_16Bit subtractor_16bit_1 (
    .B10(1'b0), .B14(1'b0), .B2(1'b0), .B6(1'b0), .A10(A10), .A14(A14), .A2(A2), .A6(A6), .B3(1'b0),
    .B7(1'b0), .B11(1'b0), .A3(A3), .A7(A7), .B15(1'b0), .A11(A11), .A15(A15), .B8(1'b0), .A8(A8), .A12(A12),
    .B12(1'b0), .A0(A0), .B0(1'b1), .A4(A4), .B4(1'b0), .B9(1'b0), .A9(A9), .A13(A13), .B13(1'b0), .A1(A1),
    .B1(1'b0), .A5(A5), .B5(1'b0), .D9(D9), .D13(D13), .D1(D1), .D5(D5), .D10(D10), .D14(D14), .D2(D2),
    .D6(D6), .D3(D3), .D7(D7), .D11(D11), .D15(D15), .Bout(Bout), .Overflow(Overflow), .D8(D8), .D12(D12),
    .D0(D0), .D4(D4));
endmodule

module SHL_4Bit (
  input  [3:0] A,
  output [3:0] Result,
  output Carry
);


  assign Carry = A[3];
  assign Result = {A[2:0], 1'b0};
endmodule

module SHL_8Bit (
  input  [7:0] A,
  output [7:0] Result,
  output Carry
);


  assign Carry = A[7];
  assign Result = {A[6:0], 1'b0};
endmodule

module SHL_16Bit (
  input  [15:0] A,
  output [15:0] Result,
  output Carry
);


  assign Carry = A[15];
  assign Result = {A[14:0], 1'b0};
endmodule

module SHR_4Bit (
  input  [3:0] A,
  output Carry,
  output [3:0] Result
);


  assign Carry = A[0];
  assign Result = {1'b0, A[3:1]};
endmodule

module SHR_8Bit (
  input  [7:0] A,
  output Carry,
  output [7:0] Result
);


  assign Carry = A[0];
  assign Result = {1'b0, A[7:1]};
endmodule

module SHR_16Bit (
  input  [15:0] A,
  output Carry,
  output [15:0] Result
);


  assign Carry = A[0];
  assign Result = {1'b0, A[15:1]};
endmodule

module Half_Subtractor (
  input  A,
  input  B,
  output Diff,
  output Borrow
);

  wire not_1_out;

  not not_1 (not_1_out, A);
  xor xor_1 (Diff, A, B);
  and and_1 (Borrow, B, not_1_out);
endmodule

module Full_Subtractor (
  input  A,
  input  B,
  input  Bin,
  output Diff,
  output Bout
);

  wire half_subtractor_1_borrow, half_subtractor_1_diff, half_subtractor_2_borrow;

  Half_Subtractor half_subtractor_1 (.A(A), .B(B), .Diff(half_subtractor_1_diff), .Borrow(half_subtractor_1_borrow));
  Half_Subtractor half_subtractor_2 (
    .A(half_subtractor_1_diff), .B(Bin), .Diff(Diff), .Borrow(half_subtractor_2_borrow));
  or or_1 (Bout, half_subtractor_2_borrow, half_subtractor_1_borrow);
endmodule

module Full_Adder (
  input  A,
  input  B,
  input  Cin,
  output S,
  output Cout
);

  wire and_1_out, and_2_out, xor_1_out;

  xor xor_1 (xor_1_out, A, B);
  and and_1 (and_1_out, A, B);
  xor xor_2 (S, xor_1_out, Cin);
  and and_2 (and_2_out, xor_1_out, Cin);
  or or_1 (Cout, and_2_out, and_1_out);
endmodule
